# Fritzing sketch Untitled Sketch 2 (saved by Fritzing 0.9.3b)

parts:
  U1 = Mini-360 DC-DC Buck converter [package=THT]
  U2 = ESP32S-HiLetgo [part_number=ESP32S-HiLetgo]
  Part1 = sensor_biometrico
  Part2 = RFID-RC522-v2
  BAT1 = 12 battery [package=battery]
  Grove1 = Grove OLED 128x96
  A1 = 2 channel relay module [package=THT]
  TTP223B1 = TTP223B Capacitive Touch Sensor Module
  KY-1 = Keyes Relay [package=THT]
  S1 = Round Pushbutton

nets:
  N1: U1.IN-, S1.leg1
  N2: U1.IN+, BAT1.-
  N3: U1.OUT+, TTP223B1.SIG, KY-1.signal, KY-1.C
  GND: U1.OUT-, U2.GND, Part1.GND, Part2.GND, Grove1.GND, A1.pin_14, TTP223B1.GND, KY-1.ground
  3.3V: U2.3.3, Part2.3.3V, Grove1.VCC
  N4: U2.GPIO25, A1.pin_15
  N5: U2.GPIO26, A1.pin_16
  VIN: U2.VIN, Part1.VCC, A1.pin_13, KY-1.NO
  N6: U2.GPIO4, Part2.RST
  N7: U2.GPIO16, Part1.TX
  N8: U2.GPIO17, Part1.RX
  N9: U2.GPIO5, Part2.SDA
  N10: U2.GPIO18, Part2.SCK
  N11: U2.GPIO19, Part2.MISO
  N12: U2.GPIO21, Grove1.SDA
  N13: U2.GPIO22, Grove1.SCL
  N14: U2.GPIO23, Part2.MOSI
  N15: BAT1.+, S1.leg0
  N16: TTP223B1.VCC, KY-1.power

custom parts:
  Mini-360 DC-DC Buck converter: Mini-360 DC-DC Buck converter. Tiny buck step down voltage converter, input voltage 4.75 to 23V output 1 to 17V adjustable. Available from ebay and the like.
  ESP32S-HiLetgo: HiLetgo ESP-WROOM-32 ESP32 ESP-32S Development Board 2.4GHz Dual-Mode WiFi + Bluetooth Dual Cores Microcontroller The ESP32 integrated with Antenna switches, RF Balun, power amplifiers, low-noise amplifiers, filters, and management modules, and the entire solution occupies the least area of PCB. 2.4 GHz Wi-Fi plus Bluetooth dual-mode chip, with TSMC Ultra-low power consumption 40nm technology,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
  sensor_biometrico: Adafruit Optical Fingerprint Sensor
  RFID-RC522-v2: A simple China made RFID-RC522 Reader; do check the pin labels, as this is a MFRC522 based clone.
  12 battery: 12V lead acid type battery, like the Husqvarna YTH2448 12V 35AH battery. This is the mini version 1/4 the size of the actual battery to be closer to typical breadboard parts (around 2in wide rathher than 7in). The pads in pcb are sized to accomidate up to 14ga wire (as these batterys will deliver high currents.)
  2 channel relay module: 2 channel Relay Module 5V 12V 24V High and Low Level Trigger Relay Control With Optocoupler Two Way relays DC 5 V 12 V 24 V Volt.
  TTP223B Capacitive Touch Sensor Module: The TTP223B capacitive touch sensor module uses the TTP223B IC. The appropriate voltage is approximately 2 to 5.5 volts.
  Keyes Relay: The Keyes 5V relay module is suitable for SCM development, home appliance control. It uses a 5V~12V TIL control signal which can control DC / AC signal.
  Round Pushbutton: A generic pushbutton.
